// Logisim project reloj.circ as structural Verilog: 5 circuits, main circuit main
module main (
  input  ena,
  input  rst
);

  wire and_1_out, and_2_out, and_3_out, and_4_out, and_5_out, and_6_out, and_7_out, clock_1_out,
       contadorbcd_1_qa, contadorbcd_1_qb, contadorbcd_1_qc, contadorbcd_1_qd, contadorbcd_2_qa,
       contadorbcd_2_qb, contadorbcd_2_qc, contadorbcd_2_qd, contadorbcd_3_qa, contadorbcd_3_qb,
       contadorbcd_3_qc, contadorbcd_3_qd, contadorbcd_4_qa, contadorbcd_4_qb, contadorbcd_4_qc,
       contadorbcd_4_qd, contadorbcd_5_qa, contadorbcd_5_qb, contadorbcd_5_qc, contadorbcd_5_qd,
       contadorbcd_6_qa, contadorbcd_6_qb, contadorbcd_6_qc, contadorbcd_6_qd, decenasHS_fa, decenasHS_fb,
       decenasHS_fc, decenasHS_fd, decenasHS_fe, decenasHS_ff, decenasHS_fg, decenasMIN_fa, decenasMIN_fb,
       decenasMIN_fc, decenasMIN_fd, decenasMIN_fe, decenasMIN_ff, decenasMIN_fg, decenasSEC_fa,
       decenasSEC_fb, decenasSEC_fc, decenasSEC_fd, decenasSEC_fe, decenasSEC_ff, decenasSEC_fg, not_1_out,
       not_2_out, not_3_out, not_4_out, not_5_out, not_6_out, not_7_out, not_8_out, not_9_out, not_10_out,
       not_11_out, not_12_out, not_13_out, not_14_out, not_15_out, or_1_out, or_2_out, or_3_out, or_4_out,
       unidadesHS_fa, unidadesHS_fb, unidadesHS_fc, unidadesHS_fd, unidadesHS_fe, unidadesHS_ff,
       unidadesHS_fg, unidadesMIN_fa, unidadesMIN_fb, unidadesMIN_fc, unidadesMIN_fd, unidadesMIN_fe,
       unidadesMIN_ff, unidadesMIN_fg, unidadesSEC_fa, unidadesSEC_fb, unidadesSEC_fc, unidadesSEC_fd,
       unidadesSEC_fe, unidadesSEC_ff, unidadesSEC_fg;

  Clock clock_1 (.out(clock_1_out));
  or or_1 (or_1_out, rst, and_3_out);
  or or_2 (or_2_out, rst, and_4_out);
  or or_3 (or_3_out, rst, and_1_out);
  and and_1 (and_1_out, contadorbcd_6_qd, and_5_out);
  or or_4 (or_4_out, rst, contadorbcd_6_qc);
  and and_2 (and_2_out, not_4_out, not_5_out, not_6_out, not_7_out);
  and and_3 (and_3_out, contadorbcd_2_qb, contadorbcd_2_qc);
  and and_4 (and_4_out, contadorbcd_4_qb, contadorbcd_4_qc);
  not not_1 (not_1_out, contadorbcd_5_qa);
  not not_2 (not_2_out, contadorbcd_5_qb);
  and and_5 (and_5_out, not_1_out, not_2_out, contadorbcd_5_qc, not_3_out);
  not not_3 (not_3_out, contadorbcd_5_qd);
  and and_6 (and_6_out, not_12_out, not_13_out, not_14_out, not_15_out);
  Contadorbcd contadorbcd_1 (
    .En(ena), .Clk(clock_1_out), .Rst(rst), .QA(contadorbcd_1_qa), .QB(contadorbcd_1_qb),
    .QC(contadorbcd_1_qc), .QD(contadorbcd_1_qd));
  not not_4 (not_4_out, contadorbcd_1_qa);
  not not_5 (not_5_out, contadorbcd_1_qb);
  not not_6 (not_6_out, contadorbcd_1_qc);
  not not_7 (not_7_out, contadorbcd_1_qd);
  Contadorbcd contadorbcd_2 (
    .En(ena), .Clk(and_2_out), .Rst(or_1_out), .QA(contadorbcd_2_qa), .QB(contadorbcd_2_qb),
    .QC(contadorbcd_2_qc), .QD(contadorbcd_2_qd));
  Contadorbcd contadorbcd_3 (
    .En(ena), .Clk(and_3_out), .Rst(rst), .QA(contadorbcd_3_qa), .QB(contadorbcd_3_qb),
    .QC(contadorbcd_3_qc), .QD(contadorbcd_3_qd));
  not not_8 (not_8_out, contadorbcd_3_qa);
  not not_9 (not_9_out, contadorbcd_3_qb);
  and and_7 (and_7_out, not_8_out, not_9_out, not_10_out, not_11_out);
  not not_10 (not_10_out, contadorbcd_3_qc);
  not not_11 (not_11_out, contadorbcd_3_qd);
  not not_12 (not_12_out, contadorbcd_5_qd);
  not not_13 (not_13_out, contadorbcd_5_qc);
  not not_14 (not_14_out, contadorbcd_5_qb);
  not not_15 (not_15_out, contadorbcd_5_qa);
  Contadorbcd contadorbcd_4 (
    .En(ena), .Clk(and_7_out), .Rst(or_2_out), .QA(contadorbcd_4_qa), .QB(contadorbcd_4_qb),
    .QC(contadorbcd_4_qc), .QD(contadorbcd_4_qd));
  Contadorbcd contadorbcd_5 (
    .En(ena), .Clk(and_4_out), .Rst(or_3_out), .QA(contadorbcd_5_qa), .QB(contadorbcd_5_qb),
    .QC(contadorbcd_5_qc), .QD(contadorbcd_5_qd));
  Contadorbcd contadorbcd_6 (
    .En(ena), .Clk(and_6_out), .Rst(or_4_out), .QA(contadorbcd_6_qa), .QB(contadorbcd_6_qb),
    .QC(contadorbcd_6_qc), .QD(contadorbcd_6_qd));
  BCD_7seg unidadesSEC (
    .A(contadorbcd_1_qa), .B(contadorbcd_1_qb), .C(contadorbcd_1_qc), .D(contadorbcd_1_qd),
    .Fa(unidadesSEC_fa), .Fb(unidadesSEC_fb), .Fc(unidadesSEC_fc), .Fd(unidadesSEC_fd), .Fe(unidadesSEC_fe),
    .Ff(unidadesSEC_ff), .Fg(unidadesSEC_fg));
  BCD_7seg decenasSEC (
    .A(contadorbcd_2_qa), .B(contadorbcd_2_qb), .C(contadorbcd_2_qc), .D(contadorbcd_2_qd),
    .Fa(decenasSEC_fa), .Fb(decenasSEC_fb), .Fc(decenasSEC_fc), .Fd(decenasSEC_fd), .Fe(decenasSEC_fe),
    .Ff(decenasSEC_ff), .Fg(decenasSEC_fg));
  BCD_7seg unidadesMIN (
    .A(contadorbcd_3_qa), .B(contadorbcd_3_qb), .C(contadorbcd_3_qc), .D(contadorbcd_3_qd),
    .Fa(unidadesMIN_fa), .Fb(unidadesMIN_fb), .Fc(unidadesMIN_fc), .Fd(unidadesMIN_fd), .Fe(unidadesMIN_fe),
    .Ff(unidadesMIN_ff), .Fg(unidadesMIN_fg));
  BCD_7seg decenasMIN (
    .A(contadorbcd_4_qa), .B(contadorbcd_4_qb), .C(contadorbcd_4_qc), .D(contadorbcd_4_qd),
    .Fa(decenasMIN_fa), .Fb(decenasMIN_fb), .Fc(decenasMIN_fc), .Fd(decenasMIN_fd), .Fe(decenasMIN_fe),
    .Ff(decenasMIN_ff), .Fg(decenasMIN_fg));
  BCD_7seg unidadesHS (
    .A(contadorbcd_5_qa), .B(contadorbcd_5_qb), .C(contadorbcd_5_qc), .D(contadorbcd_5_qd),
    .Fa(unidadesHS_fa), .Fb(unidadesHS_fb), .Fc(unidadesHS_fc), .Fd(unidadesHS_fd), .Fe(unidadesHS_fe),
    .Ff(unidadesHS_ff), .Fg(unidadesHS_fg));
  BCD_7seg decenasHS (
    .A(contadorbcd_6_qa), .B(contadorbcd_6_qb), .C(contadorbcd_6_qc), .D(contadorbcd_6_qd),
    .Fa(decenasHS_fa), .Fb(decenasHS_fb), .Fc(decenasHS_fc), .Fd(decenasHS_fd), .Fe(decenasHS_fe),
    .Ff(decenasHS_ff), .Fg(decenasHS_fg));
  _7_Segment_Display u_7_segment_display_1 (
    .g(unidadesSEC_fg), .f(unidadesSEC_ff), .a(unidadesSEC_fa), .b(unidadesSEC_fb), .e(unidadesSEC_fe),
    .d(unidadesSEC_fd), .c(unidadesSEC_fc));  // open: dp
  _7_Segment_Display u_7_segment_display_2 (
    .g(decenasSEC_fg), .f(decenasSEC_ff), .a(decenasSEC_fa), .b(decenasSEC_fb), .e(decenasSEC_fe),
    .d(decenasSEC_fd), .c(decenasSEC_fc));  // open: dp
  _7_Segment_Display u_7_segment_display_3 (
    .g(unidadesMIN_fg), .f(unidadesMIN_ff), .a(unidadesMIN_fa), .b(unidadesMIN_fb), .e(unidadesMIN_fe),
    .d(unidadesMIN_fd), .c(unidadesMIN_fc));  // open: dp
  _7_Segment_Display u_7_segment_display_4 (
    .g(decenasMIN_fg), .f(decenasMIN_ff), .a(decenasMIN_fa), .b(decenasMIN_fb), .e(decenasMIN_fe),
    .d(decenasMIN_fd), .c(decenasMIN_fc));  // open: dp
  _7_Segment_Display u_7_segment_display_5 (
    .g(unidadesHS_fg), .f(unidadesHS_ff), .a(unidadesHS_fa), .b(unidadesHS_fb), .e(unidadesHS_fe),
    .d(unidadesHS_fd), .c(unidadesHS_fc));  // open: dp
  _7_Segment_Display u_7_segment_display_6 (
    .g(decenasHS_fg), .f(decenasHS_ff), .a(decenasHS_fa), .b(decenasHS_fb), .e(decenasHS_fe),
    .d(decenasHS_fd), .c(decenasHS_fc));  // open: dp
endmodule

module Sieteseg (
  input  D_3,
  input  C_2,
  input  B_1,
  input  A_0,
  output FA,
  output FB,
  output FC,
  output FD,
  output FE,
  output FF,
  output FG
);

  wire and_1_out, and_2_out, and_3_out, and_4_out, and_5_out, and_6_out, and_7_out, and_8_out, and_9_out,
       and_10_out, and_11_out, and_12_out, and_13_out, and_14_out, and_15_out, and_16_out, and_17_out,
       and_18_out, and_19_out, and_20_out, not_1_out, not_2_out, not_3_out, not_4_out;

  not not_1 (not_1_out, D_3);
  not not_2 (not_2_out, C_2);
  not not_3 (not_3_out, B_1);
  not not_4 (not_4_out, A_0);
  and and_1 (and_1_out, C_2, A_0);
  and and_2 (and_2_out, not_4_out, not_2_out);
  and and_3 (and_3_out, A_0, B_1);
  and and_4 (and_4_out, not_4_out, not_3_out);
  and and_5 (and_5_out, not_4_out, not_3_out);
  and and_6 (and_6_out, not_2_out, not_4_out);
  and and_7 (and_7_out, A_0, not_3_out, C_2);
  and and_8 (and_8_out, B_1, not_2_out);
  and and_9 (and_9_out, not_4_out, B_1);
  and and_10 (and_10_out, not_3_out, D_3);
  and and_11 (and_11_out, not_4_out, not_2_out);
  and and_12 (and_12_out, not_4_out, B_1);
  and and_13 (and_13_out, D_3, not_2_out);
  and and_14 (and_14_out, C_2, not_3_out);
  and and_15 (and_15_out, C_2, not_4_out);
  and and_16 (and_16_out, not_4_out, not_3_out);
  and and_17 (and_17_out, B_1, not_4_out);
  and and_18 (and_18_out, C_2, not_3_out);
  and and_19 (and_19_out, D_3, not_2_out);
  and and_20 (and_20_out, not_2_out, B_1);
  or or_1 (FA, B_1, D_3, and_1_out, and_2_out);
  or or_2 (FB, not_2_out, and_3_out, and_4_out);
  or or_3 (FC, A_0, C_2, and_5_out);
  or or_4 (FD, and_6_out, and_7_out, and_10_out, and_8_out, and_9_out);
  or or_5 (FE, and_11_out, and_12_out);
  or or_6 (FF, and_13_out, and_14_out, and_15_out, and_16_out);
  or or_7 (FG, and_17_out, and_18_out, and_19_out, and_20_out);
endmodule

module BCD_7seg (
  input  A,
  input  B,
  input  C,
  input  D,
  output Fa,
  output Fb,
  output Fc,
  output Fd,
  output Fe,
  output Ff,
  output Fg
);

  wire and_1_out, and_2_out, and_3_out, and_4_out, and_5_out, and_6_out, and_7_out, and_8_out, and_9_out,
       and_10_out, and_11_out, and_12_out, and_13_out, and_14_out, and_15_out, and_16_out, and_17_out,
       and_18_out, and_19_out, not_1_out, not_2_out, not_3_out, not_4_out, not_5_out, not_6_out, not_7_out,
       not_8_out, not_9_out, not_10_out, not_11_out, not_12_out, not_13_out, not_14_out, not_15_out,
       not_16_out, not_17_out, not_18_out, not_19_out, not_20_out, not_21_out, not_22_out, not_23_out,
       not_24_out;

  not not_1 (not_1_out, B);
  not not_2 (not_2_out, D);
  not not_3 (not_3_out, C);
  not not_4 (not_4_out, B);
  not not_5 (not_5_out, D);
  not not_6 (not_6_out, B);
  not not_7 (not_7_out, C);
  not not_8 (not_8_out, D);
  not not_9 (not_9_out, D);
  not not_10 (not_10_out, C);
  not not_11 (not_11_out, D);
  not not_12 (not_12_out, C);
  not not_13 (not_13_out, B);
  not not_14 (not_14_out, D);
  not not_15 (not_15_out, C);
  not not_16 (not_16_out, D);
  not not_17 (not_17_out, B);
  not not_18 (not_18_out, B);
  not not_19 (not_19_out, D);
  not not_20 (not_20_out, B);
  not not_21 (not_21_out, C);
  not not_22 (not_22_out, D);
  not not_23 (not_23_out, C);
  not not_24 (not_24_out, B);
  and and_1 (and_1_out, B, D);
  and and_2 (and_2_out, not_18_out, not_19_out);
  and and_3 (and_3_out, not_21_out, not_22_out);
  and and_4 (and_4_out, C, D);
  and and_5 (and_5_out, not_24_out, D);
  and and_6 (and_6_out, B, C);
  and and_7 (and_7_out, not_1_out, not_2_out);
  and and_8 (and_8_out, B, not_3_out, D);
  and and_9 (and_9_out, not_4_out, C);
  and and_10 (and_10_out, B, C, not_5_out);
  and and_11 (and_11_out, not_6_out, not_7_out, not_8_out);
  and and_12 (and_12_out, C, not_9_out);
  and and_13 (and_13_out, not_10_out, not_11_out);
  and and_14 (and_14_out, B, not_12_out);
  and and_15 (and_15_out, A, not_13_out);
  and and_16 (and_16_out, B, not_14_out);
  and and_17 (and_17_out, B, not_15_out);
  and and_18 (and_18_out, B, not_16_out);
  and and_19 (and_19_out, not_17_out, C);
  or or_1 (Fa, C, A, and_1_out, and_2_out);
  or or_2 (Fb, not_20_out, and_3_out, and_4_out);
  or or_3 (Fc, not_23_out, and_5_out, and_6_out);
  or or_4 (Fd, and_7_out, and_8_out, and_9_out, and_10_out);
  or or_5 (Fe, and_11_out, and_12_out);
  or or_6 (Ff, and_13_out, and_14_out, and_15_out, and_16_out);
  or or_7 (Fg, A, and_17_out, and_18_out, and_19_out);
endmodule

module mux (
  input  D,
  input  En,
  input  Clk,
  input  Rst,
  output Q
);

  wire multiplexer_1_out;

  Multiplexer multiplexer_1 (.in0(Q), .in1(D), .out(multiplexer_1_out), .sel(En));
  D_Flip_Flop d_ff_1 (.D(multiplexer_1_out), .clk(Clk), .Q(Q), .reset(Rst));  // open: Qn, preset
endmodule

module Contadorbcd (
  input  En,
  input  Clk,
  input  Rst,
  output QA,
  output QB,
  output QC,
  output QD
);

  wire and_1_out, and_2_out, and_3_out, and_4_out, and_5_out, and_6_out, and_7_out, bcd_7seg_1_fa,
       bcd_7seg_1_fb, bcd_7seg_1_fc, bcd_7seg_1_fd, bcd_7seg_1_fe, bcd_7seg_1_ff, bcd_7seg_1_fg, not_1_out,
       not_2_out, not_3_out, not_4_out, not_5_out, not_6_out, or_1_out, or_2_out, or_3_out, undriven,
       undriven_2, undriven_3, undriven_4;

  or or_1 (or_1_out, and_1_out, and_2_out);
  and and_1 (and_1_out, QD, QC, QB);
  and and_2 (and_2_out, not_1_out, QA);
  not not_1 (not_1_out, QD);
  mux A (.D(or_1_out), .En(En), .Clk(Clk), .Rst(Rst), .Q(QA));
  LED led_1 (.in(QA));
  or or_2 (or_2_out, and_3_out, and_4_out, and_5_out);
  and and_3 (and_3_out, QD, QC, not_2_out);
  not not_2 (not_2_out, QB);
  and and_4 (and_4_out, not_6_out, QB);
  not not_3 (not_3_out, QC);
  and and_5 (and_5_out, not_3_out, QB);
  mux B (.D(or_2_out), .En(En), .Clk(Clk), .Rst(Rst), .Q(QB));
  LED led_2 (.in(QB));
  or or_3 (or_3_out, and_6_out, and_7_out);
  and and_6 (and_6_out, QD, not_4_out, not_5_out);
  not not_4 (not_4_out, QC);
  not not_5 (not_5_out, QA);
  and and_7 (and_7_out, not_6_out, QC);
  mux C (.D(or_3_out), .En(En), .Clk(Clk), .Rst(Rst), .Q(QC));
  LED led_3 (.in(QC));
  BCD_7seg bcd_7seg_1 (
    .A(undriven), .B(undriven_2), .C(undriven_3), .D(undriven_4), .Fa(bcd_7seg_1_fa), .Fb(bcd_7seg_1_fb),
    .Fc(bcd_7seg_1_fc), .Fd(bcd_7seg_1_fd), .Fe(bcd_7seg_1_fe), .Ff(bcd_7seg_1_ff), .Fg(bcd_7seg_1_fg));
  not not_6 (not_6_out, QD);
  _7_Segment_Display u_7_segment_display_1 (
    .g(bcd_7seg_1_fg), .f(bcd_7seg_1_ff), .a(bcd_7seg_1_fa), .b(bcd_7seg_1_fb), .e(bcd_7seg_1_fe),
    .d(bcd_7seg_1_fd), .c(bcd_7seg_1_fc));  // open: dp
  mux D (.D(not_6_out), .En(En), .Clk(Clk), .Rst(Rst), .Q(QD));
  LED led_4 (.in(QD));
endmodule
